// Logisim project x69_lamda_b01.circ as structural Verilog
module main (
);

  wire aludecoder_1_flagen, aludecoder_1_ien, and_1_out, and_2_out, and_3_out, and_4_out, bitfinder_1_found,
       buffer_1_out, buffer_2_out, buffer_3_out, buffer_4_out, buffer_5_out, buffer_6_out, buffer_7_out,
       button_1_out, button_2_out, clock_1_out, decoder_1_out0, decoder_1_out1, decoder_1_out2,
       decoder_1_out3, decoder_2_out0, decoder_2_out1, decoder_2_out2, memio_1_done, memio_1_mclk,
       memio_1_men, memio_1_mr, memio_1_mw, memio_2_mclk, memio_3_done, memio_3_mclk, memio_3_mr, memio_3_mw,
       not_1_out, not_2_out, not_3_out, not_4_out, not_5_out, not_6_out, not_7_out, not_8_out, or_1_out,
       or_2_out, por_1_out, por_2_out, pull_resistor_4_node, s_r_ff_1_q, switch_1_p2, t_ff_1_q, t_ff_1_qn,
       undriven, undriven_2;
  wire [0:0] register_4_q;
  wire [1:0] bitfinder_1_index, counter_1_q;
  wire [3:0] aludecoder_1_ra, aludecoder_1_rb, aludecoder_1_rd, pull_resistor_1_node, pull_resistor_2_node,
       pull_resistor_3_node;
  wire [4:0] aludecoder_1_op, register_4_q_2;
  wire [5:0] alu_1_flg;
  wire [15:0] alu_1_q, aludecoder_1_im, counter_2_q, memio_1_maddr, memio_1_mdin, memio_2_maddr,
       memio_3_dout, memio_3_maddr, memio_3_mdin, multiplexer_1_out, pull_resistor_5_node,
       pull_resistor_6_node, pull_resistor_8_node, ram_1_dout, register_1_q, register_2_q, register_3_q,
       rom_1_data;
  wire [63:0] cpuregs_1_out_7;

  Button button_1 (.out(button_1_out));
  Clock clock_1 (.out(clock_1_out));
  POR #(.PorHighDuration(1)) por_1 (.out(por_1_out));
  T_Flip_Flop t_ff_1 (.clk(button_1_out), .T(1'b1), .Q(t_ff_1_q), .Qn(t_ff_1_qn), .reset(por_1_out));  // open: preset
  S_R_Flip_Flop s_r_ff_1 (
    .S(t_ff_1_q), .clk(clock_1_out), .R(t_ff_1_qn), .Q(s_r_ff_1_q), .reset(por_1_out));  // open: Qn, preset
  not not_1 (not_1_out, s_r_ff_1_q);
  not not_2 (not_2_out, not_1_out);
  BitFinder #(.width(4)) bitfinder_1 (.in(register_1_q[3:0]), .index(bitfinder_1_index), .found(bitfinder_1_found));
  and and_1 (and_1_out, clock_1_out, s_r_ff_1_q);
  and and_2 (and_2_out, not_2_out, not_1_out);
  Decoder #(.select(2)) decoder_1 (
    .out0(decoder_1_out0), .out1(decoder_1_out1), .out2(decoder_1_out2), .out3(decoder_1_out3),
    .sel(bitfinder_1_index), .en(bitfinder_1_found));
  or or_1 (or_1_out, and_2_out, por_1_out);
  Button button_2 (.out(button_2_out));
  // Probe on pull_resistor_2_node
  // Probe on pull_resistor_3_node
  // Probe on pull_resistor_1_node
  Decoder #(.select(2)) decoder_2 (
    .out0(decoder_2_out0), .out1(decoder_2_out1), .out2(decoder_2_out2), .sel(counter_1_q), .en(button_2_out));  // open: out3
  Counter #(.max('h3), .trigger("falling"), .width(2)) counter_1 (
    .Q(counter_1_q), .clk(button_2_out));  // open: load, D, count, carry, up, clr
  Pull_Resistor #(.pull(1)) pull_resistor_1 (.node(pull_resistor_1_node));
  Pull_Resistor #(.pull(1)) pull_resistor_2 (.node(pull_resistor_2_node));
  Transistor #(.\type ("n"), .width(4)) transistor_1 (
    .in(aludecoder_1_ra), .out(pull_resistor_2_node), .gate(decoder_1_out0));
  Pull_Resistor #(.pull(1)) pull_resistor_3 (.node(pull_resistor_3_node));
  or or_2 (or_2_out, decoder_2_out1, decoder_2_out0);
  Transistor #(.gate("br"), .\type ("n"), .width(4)) transistor_2 (
    .in(aludecoder_1_rd), .out(pull_resistor_1_node), .gate(decoder_1_out0));
  D_Flip_Flop d_ff_1 (.D(undriven));  // open: clk, Q, Qn, preset, reset
  Counter #(.max('hffff), .trigger("falling"), .width(16)) counter_2 (
    .D({16{1'b0}}), .count(1'b1), .Q(counter_2_q), .up(1'b1), .clk(or_2_out), .clr(undriven_2));  // open: load, carry
  // Probe on {register_2_q, register_1_q}
  // Probe on aludecoder_1_rd
  CPURegs cpuregs_1 (
    .out_7(cpuregs_1_out_7), .in_4({{8{1'b0}}, pull_resistor_3_node, pull_resistor_2_node}), .in_5(1'b1),
    .in_6(pull_resistor_4_node), .in_1(pull_resistor_8_node), .in_2(pull_resistor_1_node), .in_3(and_4_out));
  Pull_Resistor pull_resistor_4 (.node(pull_resistor_4_node));
  not not_3 (not_3_out, decoder_2_out2);
  // Probe on aludecoder_1_rb
  Transistor #(.gate("br"), .\type ("n"), .width(4)) transistor_3 (
    .in(aludecoder_1_rb), .out(pull_resistor_3_node), .gate(not_4_out));
  // Probe on cpuregs_1_out_7
  Pull_Resistor #(.pull(1)) pull_resistor_5 (.node(pull_resistor_5_node));
  Transistor #(.\type ("n"), .width(16)) transistor_4 (.in(counter_2_q), .out(pull_resistor_5_node), .gate(not_3_out));
  Pull_Resistor #(.pull(1)) pull_resistor_6 (.node(pull_resistor_6_node));
  ALUDecoder aludecoder_1 (
    .FlagEn(aludecoder_1_flagen), .Op(aludecoder_1_op), .rA(aludecoder_1_ra), .rB(aludecoder_1_rb),
    .IEn(aludecoder_1_ien), .rD(aludecoder_1_rd), .Im(aludecoder_1_im), .Ins({register_2_q, register_1_q}));
  // Probe on pull_resistor_5_node
  not not_4 (not_4_out, aludecoder_1_ien);
  Multiplexer #(.enable("false"), .width(16)) multiplexer_1 (
    .in0(cpuregs_1_out_7[31:16]), .in1(aludecoder_1_im), .out(multiplexer_1_out), .sel(aludecoder_1_ien));
  Register #(.trigger("falling"), .width(16)) register_1 (
    .D(pull_resistor_6_node), .en(1'b1), .Q(register_1_q), .clk(decoder_2_out0), .clr(undriven_2));
  Register #(.trigger("falling"), .width(16)) register_2 (
    .D(pull_resistor_6_node), .en(1'b1), .Q(register_2_q), .clk(decoder_2_out1), .clr(undriven_2));
  // Probe on alu_1_q
  // Probe on aludecoder_1_op
  Pull_Resistor pull_resistor_7 (.node({register_2_q, register_1_q}));
  ALU alu_1 (
    .Q(alu_1_q), .Flg(alu_1_flg), .Cin(register_4_q[0]), .En(1'b1), .A(cpuregs_1_out_7[15:0]),
    .B(multiplexer_1_out), .Op(aludecoder_1_op));
  and and_3 (and_3_out, decoder_2_out2, decoder_1_out0);
  not not_5 (not_5_out, aludecoder_1_flagen);
  // Probe on {register_2_q, register_1_q}
  // Probe on pull_resistor_6_node
  Register #(.width(16)) register_3 (
    .D(alu_1_q), .en(decoder_1_out0), .Q(register_3_q), .clk(and_3_out), .clr(por_2_out));
  Register #(.width(6)) register_4 (
    .D(alu_1_flg), .en(not_5_out), .Q({register_4_q_2, register_4_q[0]}), .clk(and_3_out), .clr(por_2_out));
  POR #(.PorHighDuration(1)) por_2 (.out(por_2_out));
  not not_6 (not_6_out, and_3_out);
  not not_7 (not_7_out, not_6_out);
  Pull_Resistor #(.pull(1)) pull_resistor_8 (.node(pull_resistor_8_node));
  Transistor #(.\type ("n"), .width(16)) transistor_5 (
    .in(register_3_q), .out(pull_resistor_8_node), .gate(decoder_1_out0));
  // Probe on pull_resistor_8_node
  and and_4 (and_4_out, not_7_out, not_6_out);
  // Switch switch_1: pin names not known; wires that end beside it: 1'b1, switch_1_p2
  Pull_Resistor pull_resistor_9 (.node(switch_1_p2));
  not not_8 (not_8_out, switch_1_p2);
  MemIO memio_1 (
    .Done(memio_1_done), .DOut(pull_resistor_6_node), .MClk(memio_1_mclk), .MAddr(memio_1_maddr),
    .MDin(memio_1_mdin), .MR(memio_1_mr), .MW(memio_1_mw), .MEn(memio_1_men), .En(switch_1_p2),
    .Clk(or_2_out), .Addr(pull_resistor_5_node), .DIn(pull_resistor_6_node), .Read(or_2_out), .Write(1'b0),
    .MDn(memio_3_done), .MDout(memio_3_dout));
  MemIO memio_2 (
    .Done(memio_1_done), .DOut(pull_resistor_6_node), .MClk(memio_2_mclk), .MAddr(memio_2_maddr),
    .En(not_8_out), .Clk(or_2_out), .Addr(pull_resistor_5_node), .DIn(pull_resistor_6_node), .Read(or_2_out),
    .Write(1'b0), .MDn(buffer_3_out), .MDout(rom_1_data));  // open: MDin, MR, MW, MEn
  buf buffer_1 (buffer_1_out, memio_2_mclk);
  buf buffer_2 (buffer_2_out, buffer_1_out);
  ROM #(.dataWidth(16)) rom_1 (.addr(memio_2_maddr[7:0]), .data(rom_1_data));
  buf buffer_3 (buffer_3_out, buffer_2_out);
  MemIO memio_3 (
    .Done(memio_3_done), .DOut(memio_3_dout), .MClk(memio_3_mclk), .MAddr(memio_3_maddr),
    .MDin(memio_3_mdin), .MR(memio_3_mr), .MW(memio_3_mw), .En(memio_1_men), .Clk(memio_1_mclk),
    .Addr(memio_1_maddr), .DIn(memio_1_mdin), .Read(memio_1_mr), .Write(memio_1_mw), .MDn(buffer_7_out),
    .MDout(ram_1_dout));  // open: MEn
  buf buffer_4 (buffer_4_out, memio_3_mclk);
  buf buffer_5 (buffer_5_out, buffer_4_out);
  buf buffer_6 (buffer_6_out, buffer_5_out);
  buf buffer_7 (buffer_7_out, buffer_6_out);
  RAM #(.addrWidth(16), .dataWidth(16)) ram_1 (
    .addr(memio_3_maddr), .we(memio_3_mw), .oe(memio_3_mr), .clk(memio_3_mclk), .din(memio_3_mdin),
    .dout(ram_1_dout));

  // Notes on the sheet:
  //   Addr
  //   Data
  //   Ins
  //   Clk
  //   Clk
  //   Rb
  //   Ra
  //   Rd
  //   Write Result
  //   PC
  //   Instruction
  //   ALU Enable
  //   Clk
  //   rD
  //   No Flags
  //   Op Code
  //   rB
  //   Immediate
  //   rA
  //   Use Immediate
  //   Use Immediate
  //   Clk
  //   Op Code
  //   Clk
  //   ALU En
  //   Write Result
  //   ALU Result
  //   ALU Flags
  //   Addr
  //   Ins
  //   Data
  //   Boot Loader
  //   IO "Delay"
  //   contents of rom_1 (hex, n*v repeats v):
  //   4b 5 114b 0 41 1 11b9 1 11b9 1 1141 1 1141 1 1141 1 1141 1 1141 1 1141 1 1141 1 1141 1 1141 1 1141 1
  //   1141 1 ce92 c54a d390 3eb3 b044 31f5 5bf 5480 3de3 9d73 bb48 da7d 8d79 243b c1af 7d61 bcba c527 978d
  //   6589 a8ff 8d44 563f 5e42 7993 7a7e 87f2 38c6 e833 6a7c 2253 154c cdf8 d24d 7540 5b02 fe4b 31c0 2e77
  //   164d f1fb f11f 25fa dc14 c2d7 8560 2476 2e95 cff6 b473 4c2a 45db 6cca b4dc ef8f 6fe0 d543 afec 59c
  //   74da 67fc 20b4 cc5d 57cb c0e0 518f a5b0 cb8b a320 3b04 91da fe8d dd2e 9753 8655 3cd8 2484 a9cd 71a
  //   f4e4 c63a ff91 bdf 1b3b 6c36 316 2baa be81 da4e 4512 fdd5 f368 aa54 b655 72a9 8361 b6ad 6dc d4d0
  //   faa4 18a9 f9c4 1305 a7cf aeb6 b2e8 a41b c215 d6d3 fd8d b97e 780c ffe1 ea6d d3b1 f1b1 8097 39fa 1b45
  //   f9d7 a138 1d72 f5af c697 562e 690a 2271 4348 f159 4ab7 a076 f200 369b 9f28 af90 6bc4 321c a848 5d00
  //   3f11 dc5e 1d8 360e 48f5 b554 7833 672a 1731 c51a ce8e cb41 af13 da69 7441 33ee 95b5 ecf4 bf1f 9a4c
  //   d8e4 80ac aa4 6fe3 5d0a ece 5c6e 112d f13b 5ea5 1cf7 6e6a c8a9 6aa2 7b38 85a4 74ea c2c1 1211 d060
  //   6873 2b96 f240 82cc 4960 9e20 d276 7f49 eb53 6796 942e 6a8e f177 5e65 b670 f843 c03e 5a8d 9ad1 984c
  //   3f1b 7c5 8421 4831 bde9 ef8a fcbc bc66 3dd2 34c9 5b07 8f6 12ce e260 9954 ba81 d75c 1d67 d1d1 25ad
  //   9860 c4a0 c2c1 eeab e0dd
  //   Outside World Memory Interface
  //   Memory IO "Delay"
  //   RAM
endmodule

module Reg16 (
  input  [15:0] DIn,
  input  W,
  input  En,
  input  [3:0] Wsel,
  input  Rst,
  input  [3:0] Rs0,
  input  [3:0] Rs1,
  input  [3:0] Rs2,
  input  [3:0] Rs3,
  output [15:0] Ro0,
  output [15:0] Ro1,
  output [15:0] Ro2,
  output [15:0] Ro3
);

  wire decoder_1_out0, decoder_1_out1, decoder_1_out2, decoder_1_out3, decoder_1_out4, decoder_1_out5,
       decoder_1_out6, decoder_1_out7, decoder_1_out8, decoder_1_out9, decoder_1_out10, decoder_1_out11,
       decoder_1_out12, decoder_1_out13, decoder_1_out14, decoder_1_out15;
  wire [15:0] register_1_q, register_2_q, register_3_q, register_4_q, register_5_q, register_6_q,
       register_7_q, register_8_q, register_9_q, register_10_q, register_11_q, register_12_q, register_13_q,
       register_14_q, register_15_q, register_16_q;

  Decoder #(.select(4)) decoder_1 (
    .out0(decoder_1_out0), .out1(decoder_1_out1), .out2(decoder_1_out2), .out3(decoder_1_out3),
    .out4(decoder_1_out4), .out5(decoder_1_out5), .out6(decoder_1_out6), .out7(decoder_1_out7),
    .out8(decoder_1_out8), .out9(decoder_1_out9), .out10(decoder_1_out10), .out11(decoder_1_out11),
    .out12(decoder_1_out12), .out13(decoder_1_out13), .out14(decoder_1_out14), .out15(decoder_1_out15),
    .sel(Wsel), .en(En));
  Register #(.width(16)) register_1 (.D(DIn), .en(decoder_1_out0), .Q(register_1_q), .clk(W), .clr(Rst));
  Register #(.width(16)) register_2 (.D(DIn), .en(decoder_1_out1), .Q(register_2_q), .clk(W), .clr(Rst));
  Register #(.width(16)) register_3 (.D(DIn), .en(decoder_1_out2), .Q(register_3_q), .clk(W), .clr(Rst));
  Register #(.width(16)) register_4 (.D(DIn), .en(decoder_1_out3), .Q(register_4_q), .clk(W), .clr(Rst));
  Register #(.width(16)) register_5 (.D(DIn), .en(decoder_1_out4), .Q(register_5_q), .clk(W), .clr(Rst));
  Register #(.width(16)) register_6 (.D(DIn), .en(decoder_1_out5), .Q(register_6_q), .clk(W), .clr(Rst));
  Register #(.width(16)) register_7 (.D(DIn), .en(decoder_1_out6), .Q(register_7_q), .clk(W), .clr(Rst));
  Register #(.width(16)) register_8 (.D(DIn), .en(decoder_1_out7), .Q(register_8_q), .clk(W), .clr(Rst));
  Register #(.width(16)) register_9 (.D(DIn), .en(decoder_1_out8), .Q(register_9_q), .clk(W), .clr(Rst));
  Register #(.width(16)) register_10 (.D(DIn), .en(decoder_1_out9), .Q(register_10_q), .clk(W), .clr(Rst));
  Register #(.width(16)) register_11 (.D(DIn), .en(decoder_1_out10), .Q(register_11_q), .clk(W), .clr(Rst));
  Register #(.width(16)) register_12 (.D(DIn), .en(decoder_1_out11), .Q(register_12_q), .clk(W), .clr(Rst));
  Register #(.width(16)) register_13 (.D(DIn), .en(decoder_1_out12), .Q(register_13_q), .clk(W), .clr(Rst));
  Register #(.width(16)) register_14 (.D(DIn), .en(decoder_1_out13), .Q(register_14_q), .clk(W), .clr(Rst));
  Register #(.width(16)) register_15 (.D(DIn), .en(decoder_1_out14), .Q(register_15_q), .clk(W), .clr(Rst));
  Register #(.width(16)) register_16 (.D(DIn), .en(decoder_1_out15), .Q(register_16_q), .clk(W), .clr(Rst));
  Multiplexer #(.enable("false"), .select(4), .width(16)) multiplexer_1 (
    .in0(register_1_q), .in1(register_2_q), .in2(register_3_q), .in3(register_4_q), .in4(register_5_q),
    .in5(register_6_q), .in6(register_7_q), .in7(register_8_q), .in8(register_9_q), .in9(register_10_q),
    .in10(register_11_q), .in11(register_12_q), .in12(register_13_q), .in13(register_14_q),
    .in14(register_15_q), .in15(register_16_q), .out(Ro0), .sel(Rs0));
  Multiplexer #(.enable("false"), .select(4), .width(16)) multiplexer_2 (
    .in0(register_1_q), .in1(register_2_q), .in2(register_3_q), .in3(register_4_q), .in4(register_5_q),
    .in5(register_6_q), .in6(register_7_q), .in7(register_8_q), .in8(register_9_q), .in9(register_10_q),
    .in10(register_11_q), .in11(register_12_q), .in12(register_13_q), .in13(register_14_q),
    .in14(register_15_q), .in15(register_16_q), .out(Ro1), .sel(Rs1));
  Multiplexer #(.enable("false"), .select(4), .width(16)) multiplexer_3 (
    .in0(register_1_q), .in1(register_2_q), .in2(register_3_q), .in3(register_4_q), .in4(register_5_q),
    .in5(register_6_q), .in6(register_7_q), .in7(register_8_q), .in8(register_9_q), .in9(register_10_q),
    .in10(register_11_q), .in11(register_12_q), .in12(register_13_q), .in13(register_14_q),
    .in14(register_15_q), .in15(register_16_q), .out(Ro2), .sel(Rs2));
  Multiplexer #(.enable("false"), .select(4), .width(16)) multiplexer_4 (
    .in0(register_1_q), .in1(register_2_q), .in2(register_3_q), .in3(register_4_q), .in4(register_5_q),
    .in5(register_6_q), .in6(register_7_q), .in7(register_8_q), .in8(register_9_q), .in9(register_10_q),
    .in10(register_11_q), .in11(register_12_q), .in12(register_13_q), .in13(register_14_q),
    .in14(register_15_q), .in15(register_16_q), .out(Ro3), .sel(Rs3));
endmodule

module ALU (
  input  En,
  input  [15:0] A,
  input  [15:0] B,
  input  [4:0] Op,
  input  Cin,
  output [5:0] Flg,
  output [15:0] Q
);

  wire adder_3_cout, adder_4_cout, adder_5_cout, adder_6_cout, adder_7_cout, adder_8_cout, adder_9_cout,
       adder_10_cout, adder_11_cout, bitfinder_1_found, multiplexer_2_out, multiplexer_3_out, nor_2_out,
       nor_3_out, nor_4_out, not_7_out;
  wire [2:0] and_2_out;
  wire [3:0] pla_2_out, pla_3_out;
  wire [4:0] adder_1_out, bit_extender_1_out, shifter_1_out;
  wire [5:0] pla_1_out;
  wire [15:0] adder_2_out, adder_3_out, adder_4_out, adder_5_out, adder_6_out, adder_7_out, adder_8_out,
       adder_9_out, adder_10_out, adder_11_out, and_1_out, multiplexer_1_out, nand_1_out, nor_1_out,
       not_1_out, not_2_out, not_3_out, not_4_out, not_5_out, not_6_out, or_1_out, xnor_1_out, xor_1_out;

  assign bit_extender_1_out = {{1{1'b0}}, Op[3:0]};  // Bit_Extender bit_extender_1
  Shifter #(.width(5)) shifter_1 (.in(bit_extender_1_out), .\dist (3'b001), .out(shifter_1_out));
  assign not_1_out = ~A;  // NOT_Gate not_1, 16 bits wide
  assign not_2_out = ~A;  // NOT_Gate not_2, 16 bits wide
  assign not_3_out = ~B;  // NOT_Gate not_3, 16 bits wide
  Adder #(.width(5)) adder_1 (.a({5{1'b0}}), .b(shifter_1_out), .out(adder_1_out), .cin(Op[4]));  // open: cout
  Adder #(.width(16)) adder_2 (.a(not_2_out), .b(16'h1), .out(adder_2_out), .cin(1'b0));  // open: cout
  assign and_1_out = A & B;  // AND_Gate and_1, 16 bits wide
  assign nand_1_out = ~(A & B);  // NAND_Gate nand_1, 16 bits wide
  assign or_1_out = A | B;  // OR_Gate or_1, 16 bits wide
  assign nor_1_out = ~(A | B);  // NOR_Gate nor_1, 16 bits wide
  assign xor_1_out = A ^ B;  // XOR_Gate xor_1, 16 bits wide
  assign xnor_1_out = ~(A ^ B);  // XNOR_Gate xnor_1, 16 bits wide
  Adder #(.width(16)) adder_3 (.a(A), .b(B), .out(adder_3_out), .cin(1'b0), .cout(adder_3_cout));
  Adder #(.width(16)) adder_4 (.a(A), .b(B), .out(adder_4_out), .cin(Cin), .cout(adder_4_cout));
  Adder #(.width(16)) adder_5 (.a(not_3_out), .b(16'h1), .out(adder_5_out), .cout(adder_5_cout));  // open: cin
  Adder #(.width(16)) adder_6 (.a(not_3_out), .b(16'h1), .out(adder_6_out), .cin(Cin), .cout(adder_6_cout));
  assign not_4_out = ~16'h1;  // NOT_Gate not_4, 16 bits wide
  Adder #(.width(16)) adder_7 (.a(not_4_out), .b(16'h1), .out(adder_7_out), .cout(adder_7_cout));  // open: cin
  assign not_5_out = ~A;  // NOT_Gate not_5, 16 bits wide
  assign not_6_out = ~B;  // NOT_Gate not_6, 16 bits wide
  Adder #(.width(16)) adder_8 (.a(A), .b(adder_5_out), .out(adder_8_out), .cout(adder_8_cout));  // open: cin
  Adder #(.width(16)) adder_9 (.a(A), .b(adder_6_out), .out(adder_9_out), .cout(adder_9_cout));  // open: cin
  Adder #(.width(16)) adder_10 (.a(A), .b(16'h1), .out(adder_10_out), .cout(adder_10_cout));  // open: cin
  Adder #(.width(16)) adder_11 (.a(A), .b(adder_7_out), .out(adder_11_out), .cout(adder_11_cout));  // open: cin
  // Probe on adder_1_out
  nor nor_2 (nor_2_out, adder_11_cout, adder_7_cout);
  nor nor_3 (nor_3_out, adder_8_cout, adder_5_cout);
  nor nor_4 (nor_4_out, adder_9_cout, adder_6_cout);
  PLA #(.in_width(5), .out_width(6), .\table ("00000 000000 # CLR\n10000 000000 # SER\n00001 000001 # NOT\n10001 000101 # TWO\n00010 000001 # AND\n10010 000001 # NAND\n00011 000001 # OR\n10011 000001 # NOR\n00100 000001 # XOR\n10100 000001 # XNOR\n00101 000011 # ADD\n10101 000011 # ADC\n00110 000111 # SUB\n10110 000111 # SBC\n00111 000011 # INC\n10111 000111 # DEC\n01000 000001 # MOV\n11000 000001 # MVN\n01001 000000 # SET\n11001 000000 # STN\n01010 000111 # CMP")) pla_1 (
    .in(Op), .out(pla_1_out));
  not not_7 (not_7_out, En);
  Multiplexer #(.enable("false"), .select(5), .width(16)) multiplexer_1 (
    .in0({16{1'b0}}), .in1({16{1'b1}}), .in2(not_1_out), .in3(adder_2_out), .in4(and_1_out),
    .in5(nand_1_out), .in6(or_1_out), .in7(nor_1_out), .in8(xor_1_out), .in9(xnor_1_out), .in10(adder_3_out),
    .in11(adder_4_out), .in12(adder_8_out), .in13(adder_9_out), .in14(adder_10_out), .in15(adder_11_out),
    .in16(A), .in17(not_5_out), .in18(B), .in19(not_6_out), .in20(B), .in21({16{1'b0}}), .in22({16{1'b0}}),
    .in23({16{1'b0}}), .in24({16{1'b0}}), .in25({16{1'b0}}), .in26({16{1'b0}}), .in27({16{1'b0}}),
    .in28({16{1'b0}}), .in29({16{1'b0}}), .in30({16{1'b0}}), .in31({16{1'b0}}), .out(multiplexer_1_out),
    .sel(adder_1_out));
  BitFinder #(.width(16)) bitfinder_1 (.in(multiplexer_1_out), .found(bitfinder_1_found));  // open: index
  Pull_Resistor pull_resistor_1 (.node(Q));
  and and_2 (and_2_out[0], pla_1_out[0], ~bitfinder_1_found);  // AND_Gate
  Transistor #(.width(16)) transistor_1 (.in(multiplexer_1_out), .out(Q), .gate(not_7_out));
  and and_3 (and_2_out[1], pla_1_out[1], multiplexer_2_out);
  and and_4 (and_2_out[2], pla_1_out[2], multiplexer_3_out);
  PLA #(.in_width(5), .out_width(4), .\table ("00101 0001 # ADD (ADD)\n10101 0010 # ADC (ADC)\n00110 0011 # SUB (SUB)\n10110 0100 # SBC (SBC)\n00111 0001 # INC (ADD)\n10111 0011 # DEC (SUB)\n01010 0011 # CMP (SUB)\nxxxxx 0000 # X")) pla_2 (
    .in(adder_1_out), .out(pla_2_out));
  Multiplexer #(.enable("false"), .select(4)) multiplexer_2 (
    .in0(1'b0), .in1(adder_3_cout), .in2(adder_4_cout), .in3(adder_8_cout), .in4(adder_9_cout),
    .in5(adder_10_cout), .in6(adder_11_cout), .in7(1'b0), .in8(1'b0), .in9(1'b0), .in10(1'b0), .in11(1'b0),
    .in12(1'b0), .in13(1'b0), .in14(1'b0), .in15(1'b0), .out(multiplexer_2_out), .sel(pla_2_out));
  Pull_Resistor pull_resistor_2 (.node(Flg));
  Transistor #(.gate("br"), .width(6)) transistor_2 (.in({3'b000, and_2_out}), .out(Flg), .gate(not_7_out));
  PLA #(.in_width(5), .out_width(4), .\table ("00110 0001 # SUB (SUB)\n10110 0010 # SBC (SBC)\n10111 0001 # DEC (SUB)\n01010 0001 # CMP (SUB)\nxxxxx 0000 # X")) pla_3 (
    .in(adder_1_out), .out(pla_3_out));
  Multiplexer #(.enable("false"), .select(4)) multiplexer_3 (
    .in0(1'b0), .in1(nor_3_out), .in2(nor_4_out), .in3(nor_2_out), .in4(1'b0), .in5(1'b0), .in6(1'b0),
    .in7(1'b0), .in8(1'b0), .in9(1'b0), .in10(1'b0), .in11(1'b0), .in12(1'b0), .in13(1'b0), .in14(1'b0),
    .in15(1'b0), .out(multiplexer_3_out), .sel(pla_3_out));

  // Notes on the sheet:
  //   CLR
  //   SER
  //   AND
  //   NAND
  //   NOR
  //   XNOR
  //   SBC
  //   NOT
  //   TWO
  //   OR
  //   XOR
  //   ADD
  //   ADC
  //   SUB
  //   A - B -> D
  //   A - (B + C) -> D
  //   INC
  //   DEC
  //   MOV
  //   MVN
  //   SET
  //   STN
  //   CMP
  //   Adjusts ALU op code to match x69-lamda-a01 encoding
  //   Instruction Flags
  //   Result Selection
  //   Carry Flag Selection
  //   Z
  //   C
  //   T
  //   Twos Flag Selection
endmodule

module ALUDecoder (
  input  [31:0] Ins,
  output FlagEn,
  output [4:0] Op,
  output [3:0] rA,
  output [3:0] rB,
  output IEn,
  output [3:0] rD,
  output [15:0] Im
);

  Multiplexer #(.enable("false"), .width(4)) multiplexer_1 (.in0(Ins[19:16]), .in1(Ins[15:12]), .out(rD), .sel(Ins[1]));

  assign FlagEn = Ins[2];
  assign IEn = Ins[1];
  assign Im = Ins[31:16];
  assign Op = Ins[7:3];
  assign rA = Ins[11:8];
  assign rB = Ins[15:12];

  // Notes on the sheet:
  //   Data
  //   Use Immediate
  //   No Flags
  //   Op Code
  //   rA
  //   rB/rD
  //   rD/Immediate
endmodule

module MemIO (
  input  MDn,
  input  [15:0] MDout,
  input  [15:0] Addr,
  input  [15:0] DIn,
  input  Read,
  input  Write,
  input  En,
  input  Clk,
  output Done,
  output [15:0] DOut,
  output [15:0] MAddr,
  output [15:0] MDin,
  output MR,
  output MW,
  output MEn,
  output MClk
);

  Transistor #(.gate("br"), .\type ("n"), .width(16)) transistor_1 (.in(MDout), .out(DOut), .gate(En));
  and and_1 (MR, Read, En);
  and and_2 (MW, Write, En);

  assign Done = MDn;
  assign MAddr = Addr;
  assign MClk = Clk;
  assign MDin = DIn;
  assign MEn = En;

  // Notes on the sheet:
  //   DOut: pull=up
endmodule

module ALUTester (
);

  wire button_1_out, comparator_1_eq, rgbled_1_p1;
  wire [5:0] rgbled_1_p2;
  wire [7:0] counter_1_q;
  wire [15:0] alu_1_q;
  wire [53:0] pla_1_out;

  Button button_1 (.out(button_1_out));
  PLA #(.in_width(8), .out_width(54), .\table ("00000000 000000000000000000000000000000000000000000000000000000\n00000001 000000000000001000101000000000000000010000000000000001\nxxxxxxxx 000000000000000000000000000000000000000000000000000000")) pla_1 (
    .in(counter_1_q), .out(pla_1_out));
  Counter counter_1 (.Q(counter_1_q), .clk(button_1_out));  // open: load, D, count, carry, up, clr
  // Probe on pla_1_out[15:0]
  // Probe on pla_1_out[31:16]
  // RGBLED rgbled_1: pin names not known; wires that end beside it: rgbled_1_p1, rgbled_1_p2
  // Probe on pla_1_out[37:33]
  // Probe on pla_1_out[53:38]
  ALU alu_1 (
    .Q(alu_1_q), .Flg(rgbled_1_p2), .Cin(pla_1_out[32]), .En(1'b1), .A(pla_1_out[15:0]),
    .B(pla_1_out[31:16]), .Op(pla_1_out[37:33]));
  Comparator #(.mode("unsigned"), .width(16)) comparator_1 (
    .a(pla_1_out[53:38]), .b(alu_1_q), .eq(comparator_1_eq));  // open: gt, lt
  // Probe on alu_1_q
  not not_1 (rgbled_1_p1, comparator_1_eq);
endmodule

module RegBus_Out (
  input  in_1,
  input  [15:0] in_2,
  input  [15:0] in_3,
  input  [15:0] in_4,
  input  [15:0] in_5,
  output [63:0] out_6
);

  Transistor #(.\type ("n"), .width(64)) transistor_1 (.in({in_5, in_4, in_3, in_2}), .out(out_6), .gate(in_1));
endmodule

module RegBus_Sel (
  input  in_1,
  input  [15:0] in_2,
  output [3:0] out_3,
  output [3:0] out_4,
  output [3:0] out_5,
  output [3:0] out_6
);


  assign out_3 = in_2[3:0];
  assign out_4 = in_2[7:4];
  assign out_5 = in_2[11:8];
  assign out_6 = in_2[15:12];
endmodule

module CPURegs (
  input  [15:0] in_1,
  input  [3:0] in_2,
  input  in_3,
  input  [15:0] in_4,
  input  in_5,
  input  in_6,
  output [63:0] out_7
);

  wire decoder_1_out0, decoder_1_out1;
  wire [3:0] regbus_sel_1_out_3, regbus_sel_1_out_4, regbus_sel_1_out_5, regbus_sel_1_out_6,
       regbus_sel_2_out_3, regbus_sel_2_out_4, regbus_sel_2_out_5, regbus_sel_2_out_6;
  wire [15:0] reg16_1_ro0, reg16_1_ro1, reg16_1_ro2, reg16_1_ro3, reg16_2_ro0, reg16_2_ro1, reg16_2_ro2,
       reg16_2_ro3;

  RegBus_Sel regbus_sel_1 (
    .out_3(regbus_sel_1_out_3), .out_4(regbus_sel_1_out_4), .out_5(regbus_sel_1_out_5),
    .out_6(regbus_sel_1_out_6), .in_2(in_4), .in_1(decoder_1_out0));
  RegBus_Sel regbus_sel_2 (
    .out_3(regbus_sel_2_out_3), .out_4(regbus_sel_2_out_4), .out_5(regbus_sel_2_out_5),
    .out_6(regbus_sel_2_out_6), .in_2(in_4), .in_1(decoder_1_out1));
  Decoder decoder_1 (.out0(decoder_1_out0), .out1(decoder_1_out1), .sel(in_6), .en(in_5));
  Reg16 reg16_1 (
    .Ro1(reg16_1_ro1), .Ro2(reg16_1_ro2), .Ro0(reg16_1_ro0), .Ro3(reg16_1_ro3), .DIn(in_1), .W(in_3),
    .En(decoder_1_out0), .Wsel(in_2), .Rst(1'b0), .Rs1(regbus_sel_1_out_4), .Rs0(regbus_sel_1_out_3),
    .Rs2(regbus_sel_1_out_5), .Rs3(regbus_sel_1_out_6));
  RegBus_Out regbus_out_1 (
    .out_6(out_7), .in_2(reg16_1_ro0), .in_3(reg16_1_ro1), .in_4(reg16_1_ro2), .in_5(reg16_1_ro3),
    .in_1(decoder_1_out0));
  Reg16 reg16_2 (
    .Ro1(reg16_2_ro1), .Ro2(reg16_2_ro2), .Ro0(reg16_2_ro0), .Ro3(reg16_2_ro3), .DIn(in_1), .W(in_3),
    .En(decoder_1_out1), .Wsel(in_2), .Rst(1'b0), .Rs1(regbus_sel_2_out_4), .Rs0(regbus_sel_2_out_3),
    .Rs2(regbus_sel_2_out_5), .Rs3(regbus_sel_2_out_6));
  RegBus_Out regbus_out_2 (
    .out_6(out_7), .in_2(reg16_2_ro0), .in_3(reg16_2_ro1), .in_4(reg16_2_ro2), .in_5(reg16_2_ro3),
    .in_1(decoder_1_out1));
  Pull_Resistor #(.pull(1)) pull_resistor_1 (.node(out_7));

  // Notes on the sheet:
  //   Standard Registers
  //   Interrupt Registers
endmodule
